// Digital circuit singlecycle.dig as structural Verilog
module singlecycle (
  input  clk,
  input  [31:0] d_rdat,
  input  en,
  input  [31:0] instr,
  input  d_ack,
  input  rst,
  input  d_stall,
  output [19:0] d_adr,
  output [19:0] pc,
  output [31:0] d_wdat,
  output [3:0] d_msk,
  output [30:0] test,
  output [4:0] uop,
  output busy,
  output pass,
  output fail,
  output [31:0] ir,
  output d_stb,
  output d_cyc
);

  wire add_1_c_o, and_1_out, and_2_out, and_3_out, and_8_out, boot, comparator_2_eq, comparator_3_eq,
       comparator_5_eq, comparator_6_eq, comparator_7_eq, cond, demultiplexer_5_out_0, dmem_fsm_1_en, en_ir,
       en_mem, en_pc, en_reg, en_str, en_t, LN, lt, ltu, multiplexer_12_out, mux_addr, mux_alu, mux_ares,
       mux_func, mux_pc, mux_sb, mux_sub, N, not_3_out, not_4_out, not_5_out, rd_zero, RN, rs, sub, useq, V,
       Z;
  wire [0:0] multiplexer_1_out, register_1_q;
  wire [1:0] bitextender_6_out, demultiplexer_4_out_0, demultiplexer_4_out_1, mux_br, mux_imm, mux_res;
  wire [2:0] multiplexer_15_out;
  wire [3:0] bitextender_8_out, demultiplexer_3_out_0, multiplexer_1_out_2;
  wire [7:0] demultiplexer_1_out_0, demultiplexer_1_out_1, demultiplexer_1_out_2, demultiplexer_1_out_3,
       multiplexer_2_out;
  wire [8:8] multiplexer_4_out;
  wire [15:0] multiplexer_3_out, multiplexer_6_out_2;
  wire [16:16] multiplexer_5_out;
  wire [19:0] multiplexer_6_out, multiplexer_10_out, plus_4_s;
  wire [30:0] add_1_s, multiplexer_11_out, rf_da;
  wire [31:0] and_4_out, bitextender_1_out, bitextender_2_out, bitextender_3_out, bitextender_4_out,
       bitextender_5_out, bitextender_7_out, dat0_d, demultiplexer_2_out_0, multiplexer_7_out,
       multiplexer_8_out, multiplexer_9_out, multiplexer_14_out, multiplexer_17_out, not_1_out, or_1_out,
       or_2_out, or_4_out, prog_d, res_t, rf_db, sll_out, srl_a_out, xor_1_out;
  wire [31:1] ucode_d;
  wire [32:32] srl_a_out_2;

  D_FF u_boot (.D(~rst), .C(clk), .nQ(boot));  // open: Q
  assign or_1_out = d_rdat | dat0_d;  // Or or_1, 32 bits wide
  ROM #(.AddrBits(16), .isProgramMemory("true"), .Bits(32)) prog (.A(multiplexer_6_out_2), .sel(1'b1), .D(prog_d));
  Multiplexer #(.Bits(5)) multiplexer_1 (
    .sel(mux_sb), .in_0(ir[24:20]), .in_1(ir[11:7]), .out({multiplexer_1_out_2, multiplexer_1_out[0]}));
  assign or_2_out = instr | prog_d;  // Or or_2, 32 bits wide
  dmem_fsm dmem_fsm_1 (
    .ack(d_ack), .req(and_1_out), .stall(d_stall), .C(clk), .cyc(d_cyc), .en(dmem_fsm_1_en), .stb(d_stb));
  and and_1 (and_1_out, en_mem, ~useq);  // And
  Comparator #(.Bits(5)) comparator_1 (.a(ir[11:7]), .b({5{1'b0}}), .eq(rd_zero));  // open: gt, lt
  Multiplexer #(.Selector_Bits(2), .Bits(8)) multiplexer_2 (
    .sel(d_adr[1:0]), .in_0(or_1_out[7:0]), .in_1(or_1_out[15:8]), .in_2(or_1_out[23:16]),
    .in_3(or_1_out[31:24]), .out(multiplexer_2_out));
  Multiplexer #(.Bits(16)) multiplexer_3 (
    .sel(d_adr[1]), .in_0(or_1_out[15:0]), .in_1(or_1_out[31:16]), .out(multiplexer_3_out));
  and and_2 (and_2_out, useq, d_cyc);
  Register #(.Bits(32)) u_ir (.D(or_2_out), .C(clk), .en(en_ir), .Q(ir));
  RegisterFile #(.AddrBits(5), .Bits(32)) rf (
    .Din(res_t), .we(en_reg), .Rw(ir[11:7]), .C(clk), .Ra(ir[19:15]), .Rb(ir[24:20]), .Da({LN, rf_da}),
    .Db(rf_db));
  BitExtender #(.inputBits(12), .outputBits(32)) bitextender_1 (
    .in({ir[31:25], multiplexer_1_out_2, multiplexer_1_out[0]}), .out(bitextender_1_out));
  BitExtender #(.inputBits(13), .outputBits(32)) bitextender_2 (
    .in({ir[31], multiplexer_1_out[0], ir[30:25], multiplexer_1_out_2, 1'b0}), .out(bitextender_2_out));
  Multiplexer multiplexer_4 (.sel(ir[14]), .in_0(multiplexer_2_out[7]), .in_1(1'b0), .out(multiplexer_4_out[8]));
  Multiplexer multiplexer_5 (.sel(ir[14]), .in_0(multiplexer_3_out[15]), .in_1(1'b0), .out(multiplexer_5_out[16]));
  and and_3 (and_3_out, en, ~and_2_out);  // And
  Add #(.Bits(20)) plus_4 (.a(pc), .b(20'h4), .c_i(1'b0), .s(plus_4_s));  // open: c_o
  Register #(.Bits(20)) u_pc (
    .D({multiplexer_6_out[19:18], multiplexer_6_out_2, multiplexer_6_out[1:0]}), .C(clk), .en(en_pc), .Q(pc));
  BitExtender #(.inputBits(21), .outputBits(32)) bitextender_3 (
    .in({ir[31], ir[19:12], multiplexer_1_out[0], ir[30:25], multiplexer_1_out_2, 1'b0}),
    .out(bitextender_3_out));
  BitExtender #(.inputBits(9), .outputBits(32)) bitextender_4 (
    .in({multiplexer_4_out[8], multiplexer_2_out}), .out(bitextender_4_out));
  BitExtender #(.inputBits(17), .outputBits(32)) bitextender_5 (
    .in({multiplexer_5_out[16], multiplexer_3_out}), .out(bitextender_5_out));
  uop_mapper_wrapper uop_mapper_wrapper_1 (.isnt(ir), .ack(useq), .uop(uop));
  or or_3 (en_t, and_3_out, dmem_fsm_1_en);
  Multiplexer #(.Bits(20)) multiplexer_6 (
    .sel(mux_pc), .in_0(plus_4_s), .in_1(d_adr),
    .out({multiplexer_6_out[19:18], multiplexer_6_out_2, multiplexer_6_out[1:0]}));
  Multiplexer #(.Bits(32)) multiplexer_7 (
    .sel(mux_alu), .in_0(rf_db), .in_1(bitextender_1_out), .out(multiplexer_7_out));
  Multiplexer #(.Selector_Bits(2), .Bits(32)) multiplexer_8 (
    .sel(mux_imm), .in_0(bitextender_1_out),
    .in_1({ir[31:25], multiplexer_1_out_2, multiplexer_1_out[0], ir[19:12], {12{1'b0}}}),
    .in_2(bitextender_2_out), .in_3(bitextender_3_out), .out(multiplexer_8_out));
  Multiplexer #(.Selector_Bits(2), .Bits(32)) multiplexer_9 (
    .sel(ir[13:12]), .in_0(bitextender_4_out), .in_1(bitextender_5_out), .in_2(or_1_out), .in_3(or_1_out),
    .out(multiplexer_9_out));
  ROM #(.AddrBits(5), .Bits(32)) ucode (
    .A(uop), .sel(1'b1),
    .D({ucode_d[31:25], mux_ares, mux_res, mux_imm, mux_br, mux_sb, mux_sub, ucode_d[15], mux_func, mux_alu, mux_addr, ucode_d[11:1], busy}));
  Register u_useq (.D(busy), .C(clk), .en(en_t), .Q(useq));
  Comparator comparator_2 (.a(LN), .b(RN), .eq(comparator_2_eq));  // open: gt, lt
  Multiplexer #(.Bits(20)) multiplexer_10 (.sel(mux_addr), .in_0(pc), .in_1(rf_da[19:0]), .out(multiplexer_10_out));
  Multiplexer #(.Bits(32)) multiplexer_11 (
    .sel(sub), .in_0(multiplexer_7_out), .in_1(not_1_out), .out({RN, multiplexer_11_out}));
  assign not_1_out = ~multiplexer_7_out;  // Not not_1, 32 bits wide
  BarrelShifter #(.Bits(32)) sll (.in({LN, rf_da}), .shift(multiplexer_7_out[5:0]), .out(sll_out));
  assign xor_1_out = multiplexer_7_out ^ {LN, rf_da};  // XOr xor_1, 32 bits wide
  BarrelShifter #(.Bits(33), .barrelShifterMode("arithmetic"), .direction("right")) srl_a (
    .in({rs, LN, rf_da}), .shift(multiplexer_7_out[5:0]), .out({srl_a_out_2[32], srl_a_out}));
  assign or_4_out = multiplexer_7_out | {LN, rf_da};  // Or or_4, 32 bits wide
  assign and_4_out = multiplexer_7_out & {LN, rf_da};  // And and_4, 32 bits wide
  Demultiplexer #(.Selector_Bits(2), .Bits(8)) demultiplexer_1 (
    .sel(d_adr[1:0]), .in(rf_db[7:0]), .out_0(demultiplexer_1_out_0), .out_1(demultiplexer_1_out_1),
    .out_2(demultiplexer_1_out_2), .out_3(demultiplexer_1_out_3));
  Demultiplexer #(.Bits(16)) demultiplexer_2 (
    .sel(d_adr[1]), .in(rf_db[15:0]), .out_0(demultiplexer_2_out_0[15:0]),
    .out_1(demultiplexer_2_out_0[31:16]));
  Multiplexer #(.Selector_Bits(2)) multiplexer_12 (
    .sel(mux_br), .in_0(1'b0), .in_1(1'b1), .in_2(cond), .in_3(cond), .out(multiplexer_12_out));
  Comparator comparator_3 (.a(LN), .b(N), .eq(comparator_3_eq));  // open: gt, lt
  Add #(.Bits(20)) address (.a(multiplexer_10_out), .b(multiplexer_8_out[19:0]), .c_i(1'b0), .s(d_adr));  // open: c_o
  Add #(.Bits(32)) add_1 (.a({LN, rf_da}), .b({RN, multiplexer_11_out}), .c_i(sub), .s({N, add_1_s}), .c_o(add_1_c_o));
  Comparator #(.Bits(32)) comparator_4 (.a({N, add_1_s}), .b({32{1'b0}}), .eq(Z));  // open: gt, lt
  or or_5 (mux_pc, multiplexer_12_out, boot);
  and and_5 (V, comparator_2_eq, ~comparator_3_eq);  // And
  not not_2 (ltu, add_1_c_o);
  Multiplexer #(.Selector_Bits(2), .Bits(32)) multiplexer_13 (
    .sel(ir[13:12]),
    .in_0({demultiplexer_1_out_3, demultiplexer_1_out_2, demultiplexer_1_out_1, demultiplexer_1_out_0}),
    .in_1(demultiplexer_2_out_0), .in_2(rf_db), .in_3(rf_db), .out(d_wdat));
  and and_6 (en_pc, ucode_d[6], en_t);
  and and_7 (en_reg, ucode_d[7], ~rd_zero, en_t);  // And
  Multiplexer #(.Selector_Bits(3), .Bits(32)) multiplexer_14 (
    .sel(multiplexer_15_out), .in_0({N, add_1_s}), .in_1(sll_out), .in_2({{31{1'b0}}, lt}),
    .in_3({{31{1'b0}}, ltu}), .in_4(xor_1_out), .in_5(srl_a_out), .in_6(or_4_out), .in_7(and_4_out),
    .out(multiplexer_14_out));
  Multiplexer #(.Bits(3)) multiplexer_15 (.sel(mux_func), .in_0(3'b000), .in_1(ir[14:12]), .out(multiplexer_15_out));
  Demultiplexer #(.Selector_Bits(2)) demultiplexer_3 (
    .sel(d_adr[1:0]), .in(en_str), .out_0(demultiplexer_3_out_0[0]), .out_1(demultiplexer_3_out_0[1]),
    .out_2(demultiplexer_3_out_0[2]), .out_3(demultiplexer_3_out_0[3]));
  BitExtender #(.inputBits(1), .outputBits(2)) bitextender_6 (.in(en_str), .out(bitextender_6_out));
  and and_8 (and_8_out, ~ir[7], ir[8], ~ir[9], ir[10], ~ir[11]);  // And
  BitExtender #(.inputBits(20), .outputBits(32)) bitextender_7 (.in(d_adr), .out(bitextender_7_out));
  Demultiplexer #(.Bits(2)) demultiplexer_4 (
    .sel(d_adr[1]), .in(bitextender_6_out), .out_0(demultiplexer_4_out_0), .out_1(demultiplexer_4_out_1));
  BitExtender #(.inputBits(1), .outputBits(4)) bitextender_8 (.in(en_str), .out(bitextender_8_out));
  Register #(.Bits(32)) register_1 (.D(res_t), .C(clk), .en(and_8_out), .Q({test, register_1_q[0]}));
  Comparator #(.Bits(2)) comparator_5 (.a(pc[1:0]), .b(2'b00), .eq(comparator_5_eq));  // open: gt, lt
  Comparator #(.Bits(32)) comparator_6 (
    .a({test, register_1_q[0]}), .b({32{1'b0}}), .eq(comparator_6_eq));  // open: gt, lt
  Comparator #(.Bits(5)) comparator_7 (.a(uop), .b(5'b10100), .eq(comparator_7_eq));  // open: gt, lt
  Multiplexer #(.Bits(32)) multiplexer_16 (
    .sel(mux_ares), .in_0(multiplexer_17_out), .in_1(bitextender_7_out), .out(res_t));
  Multiplexer #(.Selector_Bits(2), .Bits(32)) multiplexer_17 (
    .sel(mux_res), .in_0({{12{1'b0}}, plus_4_s}), .in_1(multiplexer_14_out), .in_2(multiplexer_8_out),
    .in_3(multiplexer_9_out), .out(multiplexer_17_out));
  xor xor_2 (lt, N, V);
  not not_3 (not_3_out, Z);
  not not_4 (not_4_out, lt);
  not not_5 (not_5_out, ltu);
  Multiplexer multiplexer_18 (.sel(ir[30]), .in_0(1'b0), .in_1(LN), .out(rs));
  Multiplexer #(.Selector_Bits(2), .Bits(4)) multiplexer_19 (
    .sel(ir[13:12]), .in_0(demultiplexer_3_out_0), .in_1({demultiplexer_4_out_1, demultiplexer_4_out_0}),
    .in_2(bitextender_8_out), .in_3(bitextender_8_out), .out(d_msk));
  and and_9 (en_str, ucode_d[8], d_stb);
  and and_10 (en_mem, ucode_d[9], en_t);
  and and_11 (en_ir, ucode_d[10], en_t);
  Multiplexer multiplexer_20 (.sel(mux_sub), .in_0(ucode_d[11]), .in_1(ir[30]), .out(sub));
  Demultiplexer demultiplexer_5 (
    .sel(comparator_6_eq), .in(comparator_7_eq), .out_0(demultiplexer_5_out_0), .out_1(pass));
  Multiplexer #(.Selector_Bits(3)) multiplexer_21 (
    .sel(ir[14:12]), .in_0(Z), .in_1(not_3_out), .in_2(1'b0), .in_3(1'b0), .in_4(lt), .in_5(not_4_out),
    .in_6(ltu), .in_7(not_5_out), .out(cond));
  or or_6 (fail, ~comparator_5_eq, demultiplexer_5_out_0);  // Or
  BlockRAMDualPort #(.AddrBits(16), .Bits(8)) dat0 (
    .A(d_adr[17:2]), .Din(d_wdat[7:0]), .str(d_msk[0]), .C(clk), .D(dat0_d[7:0]));
  BlockRAMDualPort #(.AddrBits(16), .Bits(8)) dat1 (
    .A(d_adr[17:2]), .Din(d_wdat[15:8]), .str(d_msk[1]), .C(clk), .D(dat0_d[15:8]));
  BlockRAMDualPort #(.AddrBits(16), .Bits(8)) dat2 (
    .A(d_adr[17:2]), .Din(d_wdat[23:16]), .str(d_msk[2]), .C(clk), .D(dat0_d[23:16]));
  BlockRAMDualPort #(.AddrBits(16), .Bits(8)) dat3 (
    .A(d_adr[17:2]), .Din(d_wdat[31:24]), .str(d_msk[3]), .C(clk), .D(dat0_d[31:24]));

  // Other names for the same wires on the sheet: busy_t = busy; C = clk; cyc = d_cyc; algn[1:0] = d_adr[1:0];
  //   rd[4:0] = ir[11:7]; funct3[2:0] = ir[14:12]; rs1[4:0] = ir[19:15]; rs2[4:0] = ir[24:20];
  //   funct7[6:0] = ir[31:25]; alt = ir[30]; pcalgn[1:0] = pc[1:0]; stb = d_stb

  // Notes on the sheet:
  //   en: default 1
  //   d_ack: default 1
  //   contents of prog (hex, n*v repeats v):
  //   2ec00093,ff0737,ff70713,e0a023,ff010737,f0070713,e0a223,ff01737
  //   ,ff070713,e0a423,f00ff737,f70713,e0a623,200193,ff07b7,ff78793
  //   ,2ec00093,a703,ff03b7,ff38393,26771463,300193,ff0107b7,f0078793
  //   ,2ec00093,40a703,ff0103b7,f0038393,24771463,400193,ff017b7,ff078793
  //   ,2ec00093,80a703,ff013b7,ff038393,22771463,500193,f00ff7b7,f78793
  //   ,2ec00093,c0a703,f00ff3b7,f38393,20771463,600193,ff07b7,ff78793
  //   ,2f800093,ff40a703,ff03b7,ff38393,1e771463,700193,ff0107b7,f0078793
  //   ,2f800093,ff80a703,ff0103b7,f0038393,1c771463,800193,ff017b7,ff078793
  //   ,2f800093,ffc0a703,ff013b7,ff038393,1a771463,900193,f00ff7b7,f78793
  //   ,2f800093,a703,f00ff3b7,f38393,18771463,a00193,2ec00093,fe008093
  //   ,200a283,ff03b7,ff38393,16729663,b00193,2ec00093,ffd08093,70a283
  //   ,ff0103b7,f0038393,14729863,c00193,213,2f000093,40a703,70313,ff013b7
  //   ,ff038393,12731863,120213,200293,fe5210e3,d00193,213,2f400093
  //   ,40a703,13,70313,f00ff3b7,f38393,10731063,120213,200293,fc521ee3
  //   ,e00193,213,2ec00093,40a703,13,13,70313,ff0103b7,f0038393,c731663
  //   ,120213,200293,fc521ce3,f00193,213,2f000093,40a703,ff013b7,ff038393
  //   ,a771263,120213,200293,fe5212e3,1000193,213,2f400093,13,40a703
  //   ,f00ff3b7,f38393,6771c63,120213,200293,fe5210e3,1100193,213,2ec00093
  //   ,13,13,40a703,ff0103b7,f0038393,4771463,120213,200293,fc521ee3
  //   ,1200193,2ec00293,2a103,200113,200393,2711263,1300193,2ec00293
  //   ,2a103,13,200113,200393,711463,2301063,ff0000f,18063,119193,11e193
  //   ,5d00893,18513,73,ff0000f,100193,5d00893,513,73,c0001073,ff00ff
  //   ,ff00ff00,ff00ff0,f00ff00f
  //   contents of ucode (hex, n*v repeats v):
  //   401,4144c0,404cc0,4144c0,1,1,1,4064c0,406cc0,4064c0,2a0c40,3404c0
  //   ,414c0,9004c0,4*1,440,7*1
endmodule
