// Digital circuit testbench.dig as structural Verilog
module testbench (
  input  clk,
  output pass,
  output fail,
  output [31:0] pc,
  output [30:0] testcase,
  output [4:0] uop,
  output [31:0] ir
);

  // singlecycle singlecycle_1: pin names not known; wires that end beside it: clk, {32{1'b0}}, 1'b1, {32{1'b0}}, 1'b1, pc, testcase, uop, pass, fail, ir
endmodule

/* Test case simple:
clk pass fail pc uop testcase ir

# /home/rj45/Code/rjsc5/tests/simple.hex
program(0x00100193, 0x05d00893, 0x00000513, 0x00000073, 0xc0001073)

let i = 0;
while(!(pass | fail | (i >= 2000)))
  let i = i + 1;
  0 0 0 x x x x
  1 x x x x x x
end while
0 1 0 x x x x
*/

/* Test case add:
clk pass fail pc uop testcase ir

# /home/rj45/Code/rjsc5/tests/sub.hex
program(0x00000093, 0x00000113, 0x40208733, 0x00000393, 0x4a771663, 0x00300193, 0x00100093, 0x00100113, 0x40208733, 0x00000393, 0x48771a63, 0x00400193, 0x00300093, 0x00700113, 0x40208733, 0xffc00393, 0x46771e63, 0x00500193, 0x00000093, 0xffff8137, 0x40208733, 0x000083b7, 0x46771263, 0x00600193, 0x800000b7, 0x00000113, 0x40208733, 0x800003b7, 0x44771663, 0x00700193, 0x800000b7, 0xffff8137, 0x40208733, 0x800083b7, 0x42771a63, 0x00800193, 0x00000093, 0x00008137, 0xfff10113, 0x40208733, 0xffff83b7, 0x00138393, 0x40771a63, 0x00900193, 0x800000b7, 0xfff08093, 0x00000113, 0x40208733, 0x800003b7, 0xfff38393, 0x3e771a63, 0x00a00193, 0x800000b7, 0xfff08093, 0x00008137, 0xfff10113, 0x40208733, 0x7fff83b7, 0x3c771a63, 0x00b00193, 0x800000b7, 0x00008137, 0xfff10113, 0x40208733, 0x7fff83b7, 0x00138393, 0x3a771a63, 0x00c00193, 0x800000b7, 0xfff08093, 0xffff8137, 0x40208733, 0x800083b7, 0xfff38393, 0x38771a63, 0x00d00193, 0x00000093, 0xfff00113, 0x40208733, 0x00100393, 0x36771e63, 0x00e00193, 0xfff00093, 0x00100113, 0x40208733, 0xffe00393, 0x36771263, 0x00f00193, 0xfff00093, 0xfff00113, 0x40208733, 0x00000393, 0x34771663, 0x01000193, 0x00d00093, 0x00b00113, 0x402080b3, 0x00200393, 0x32709a63, 0x01100193, 0x00e00093, 0x00b00113, 0x40208133, 0x00300393, 0x30711e63, 0x01200193, 0x00d00093, 0x401080b3, 0x00000393, 0x30709463, 0x01300193, 0x00000213, 0x00d00093, 0x00b00113, 0x40208733, 0x00070313, 0x00120213, 0x00200293, 0xfe5214e3, 0x00200393, 0x2c731e63, 0x01400193, 0x00000213, 0x00e00093, 0x00b00113, 0x40208733, 0x00000013, 0x00070313, 0x00120213, 0x00200293, 0xfe5212e3, 0x00300393, 0x2a731663, 0x01500193, 0x00000213, 0x00f00093, 0x00b00113, 0x40208733, 0x00000013, 0x00000013, 0x00070313, 0x00120213, 0x00200293, 0xfe5210e3, 0x00400393, 0x26731c63, 0x01600193, 0x00000213, 0x00d00093, 0x00b00113, 0x40208733, 0x00120213, 0x00200293, 0xfe5216e3, 0x00200393, 0x24771863, 0x01700193, 0x00000213, 0x00e00093, 0x00b00113, 0x00000013, 0x40208733, 0x00120213, 0x00200293, 0xfe5214e3, 0x00300393, 0x22771263, 0x01800193, 0x00000213, 0x00f00093, 0x00b00113, 0x00000013, 0x00000013, 0x40208733, 0x00120213, 0x00200293, 0xfe5212e3, 0x00400393, 0x1e771a63, 0x01900193, 0x00000213, 0x00d00093, 0x00000013, 0x00b00113, 0x40208733, 0x00120213, 0x00200293, 0xfe5214e3, 0x00200393, 0x1c771463, 0x01a00193, 0x00000213, 0x00e00093, 0x00000013, 0x00b00113, 0x00000013, 0x40208733, 0x00120213, 0x00200293, 0xfe5212e3, 0x00300393, 0x18771c63, 0x01b00193, 0x00000213, 0x00f00093, 0x00000013, 0x00000013, 0x00b00113, 0x40208733, 0x00120213, 0x00200293, 0xfe5212e3, 0x00400393, 0x16771463, 0x01c00193, 0x00000213, 0x00b00113, 0x00d00093, 0x40208733, 0x00120213, 0x00200293, 0xfe5216e3, 0x00200393, 0x14771063, 0x01d00193, 0x00000213, 0x00b00113, 0x00e00093, 0x00000013, 0x40208733, 0x00120213, 0x00200293, 0xfe5214e3, 0x00300393, 0x10771a63, 0x01e00193, 0x00000213, 0x00b00113, 0x00f00093, 0x00000013, 0x00000013, 0x40208733, 0x00120213, 0x00200293, 0xfe5212e3, 0x00400393, 0x0e771263, 0x01f00193, 0x00000213, 0x00b00113, 0x00000013, 0x00d00093, 0x40208733, 0x00120213, 0x00200293, 0xfe5214e3, 0x00200393, 0x0a771c63, 0x02000193, 0x00000213, 0x00b00113, 0x00000013, 0x00e00093, 0x00000013, 0x40208733, 0x00120213, 0x00200293, 0xfe5212e3, 0x00300393, 0x08771463, 0x02100193, 0x00000213, 0x00b00113, 0x00000013, 0x00000013, 0x00f00093, 0x40208733, 0x00120213, 0x00200293, 0xfe5212e3, 0x00400393, 0x04771c63, 0x02200193, 0xff100093, 0x40100133, 0x00f00393, 0x04711263, 0x02300193, 0x02000093, 0x40008133, 0x02000393, 0x02711863, 0x02400193, 0x400000b3, 0x00000393, 0x02709063, 0x02500193, 0x01000093, 0x01e00113, 0x40208033, 0x00000393, 0x00701463, 0x02301063, 0x0ff0000f, 0x00018063, 0x00119193, 0x0011e193, 0x05d00893, 0x00018513, 0x00000073, 0x0ff0000f, 0x00100193, 0x05d00893, 0x00000513, 0x00000073, 0xc0001073)

let i = 0;
while(!(pass | fail | (i >= 2000)))
  let i = i + 1;
  0 0 0 x x x x
  1 x x x x x x
end while
0 1 0 x x x x
*/

/* Test case and:
clk pass fail pc uop testcase ir

# /home/rj45/Code/rjsc5/tests/and.hex
program(0xff0100b7, 0xf0008093, 0x0f0f1137, 0xf0f10113, 0x0020f733, 0x0f0013b7, 0xf0038393, 0x48771c63, 0x00300193, 0x0ff010b7, 0xff008093, 0xf0f0f137, 0x0f010113, 0x0020f733, 0x00f003b7, 0x0f038393, 0x46771a63, 0x00400193, 0x00ff00b7, 0x0ff08093, 0x0f0f1137, 0xf0f10113, 0x0020f733, 0x000f03b7, 0x00f38393, 0x44771863, 0x00500193, 0xf00ff0b7, 0x00f08093, 0xf0f0f137, 0x0f010113, 0x0020f733, 0xf000f3b7, 0x42771863, 0x00600193, 0xff0100b7, 0xf0008093, 0x0f0f1137, 0xf0f10113, 0x0020f0b3, 0x0f0013b7, 0xf0038393, 0x40709663, 0x00700193, 0x0ff010b7, 0xff008093, 0xf0f0f137, 0x0f010113, 0x0020f133, 0x00f003b7, 0x0f038393, 0x3e711463, 0x00800193, 0xff0100b7, 0xf0008093, 0x0010f0b3, 0xff0103b7, 0xf0038393, 0x3c709663, 0x00900193, 0x00000213, 0xff0100b7, 0xf0008093, 0x0f0f1137, 0xf0f10113, 0x0020f733, 0x00070313, 0x00120213, 0x00200293, 0xfe5210e3, 0x0f0013b7, 0xf0038393, 0x38731a63, 0x00a00193, 0x00000213, 0x0ff010b7, 0xff008093, 0xf0f0f137, 0x0f010113, 0x0020f733, 0x00000013, 0x00070313, 0x00120213, 0x00200293, 0xfc521ee3, 0x00f003b7, 0x0f038393, 0x34731c63, 0x00b00193, 0x00000213, 0x00ff00b7, 0x0ff08093, 0x0f0f1137, 0xf0f10113, 0x0020f733, 0x00000013, 0x00000013, 0x00070313, 0x00120213, 0x00200293, 0xfc521ce3, 0x000f03b7, 0x00f38393, 0x30731c63, 0x00c00193, 0x00000213, 0xff0100b7, 0xf0008093, 0x0f0f1137, 0xf0f10113, 0x0020f733, 0x00120213, 0x00200293, 0xfe5212e3, 0x0f0013b7, 0xf0038393, 0x2e771263, 0x00d00193, 0x00000213, 0x0ff010b7, 0xff008093, 0xf0f0f137, 0x0f010113, 0x00000013, 0x0020f733, 0x00120213, 0x00200293, 0xfe5210e3, 0x00f003b7, 0x0f038393, 0x2a771663, 0x00e00193, 0x00000213, 0x00ff00b7, 0x0ff08093, 0x0f0f1137, 0xf0f10113, 0x00000013, 0x00000013, 0x0020f733, 0x00120213, 0x00200293, 0xfc521ee3, 0x000f03b7, 0x00f38393, 0x26771863, 0x00f00193, 0x00000213, 0xff0100b7, 0xf0008093, 0x00000013, 0x0f0f1137, 0xf0f10113, 0x0020f733, 0x00120213, 0x00200293, 0xfe5210e3, 0x0f0013b7, 0xf0038393, 0x22771c63, 0x01000193, 0x00000213, 0x0ff010b7, 0xff008093, 0x00000013, 0xf0f0f137, 0x0f010113, 0x00000013, 0x0020f733, 0x00120213, 0x00200293, 0xfc521ee3, 0x00f003b7, 0x0f038393, 0x1e771e63, 0x01100193, 0x00000213, 0x00ff00b7, 0x0ff08093, 0x00000013, 0x00000013, 0x0f0f1137, 0xf0f10113, 0x0020f733, 0x00120213, 0x00200293, 0xfc521ee3, 0x000f03b7, 0x00f38393, 0x1c771063, 0x01200193, 0x00000213, 0x0f0f1137, 0xf0f10113, 0xff0100b7, 0xf0008093, 0x0020f733, 0x00120213, 0x00200293, 0xfe5212e3, 0x0f0013b7, 0xf0038393, 0x18771663, 0x01300193, 0x00000213, 0xf0f0f137, 0x0f010113, 0x0ff010b7, 0xff008093, 0x00000013, 0x0020f733, 0x00120213, 0x00200293, 0xfe5210e3, 0x00f003b7, 0x0f038393, 0x14771a63, 0x01400193, 0x00000213, 0x0f0f1137, 0xf0f10113, 0x00ff00b7, 0x0ff08093, 0x00000013, 0x00000013, 0x0020f733, 0x00120213, 0x00200293, 0xfc521ee3, 0x000f03b7, 0x00f38393, 0x10771c63, 0x01500193, 0x00000213, 0x0f0f1137, 0xf0f10113, 0x00000013, 0xff0100b7, 0xf0008093, 0x0020f733, 0x00120213, 0x00200293, 0xfe5210e3, 0x0f0013b7, 0xf0038393, 0x0e771063, 0x01600193, 0x00000213, 0xf0f0f137, 0x0f010113, 0x00000013, 0x0ff010b7, 0xff008093, 0x00000013, 0x0020f733, 0x00120213, 0x00200293, 0xfc521ee3, 0x00f003b7, 0x0f038393, 0x0a771263, 0x01700193, 0x00000213, 0x0f0f1137, 0xf0f10113, 0x00000013, 0x00000013, 0x00ff00b7, 0x0ff08093, 0x0020f733, 0x00120213, 0x00200293, 0xfc521ee3, 0x000f03b7, 0x00f38393, 0x06771463, 0x01800193, 0xff0100b7, 0xf0008093, 0x00107133, 0x00000393, 0x04711863, 0x01900193, 0x00ff00b7, 0x0ff08093, 0x0000f133, 0x00000393, 0x02711c63, 0x01a00193, 0x000070b3, 0x00000393, 0x02709463, 0x01b00193, 0x111110b7, 0x11108093, 0x22222137, 0x22210113, 0x0020f033, 0x00000393, 0x00701463, 0x02301063, 0x0ff0000f, 0x00018063, 0x00119193, 0x0011e193, 0x05d00893, 0x00018513, 0x00000073, 0x0ff0000f, 0x00100193, 0x05d00893, 0x00000513, 0x00000073, 0xc0001073)

let i = 0;
while(!(pass | fail | (i >= 2000)))
  let i = i + 1;
  0 0 0 x x x x
  1 x x x x x x
end while
0 1 0 x x x x
*/

/* Test case or:
clk pass fail pc uop testcase ir

# /home/rj45/Code/rjsc5/tests/or.hex
program(0xff0100b7, 0xf0008093, 0x0f0f1137, 0xf0f10113, 0x0020e733, 0xff1003b7, 0xf0f38393, 0x4a771263, 0x00300193, 0x0ff010b7, 0xff008093, 0xf0f0f137, 0x0f010113, 0x0020e733, 0xfff103b7, 0xff038393, 0x48771063, 0x00400193, 0x00ff00b7, 0x0ff08093, 0x0f0f1137, 0xf0f10113, 0x0020e733, 0x0fff13b7, 0xfff38393, 0x44771e63, 0x00500193, 0xf00ff0b7, 0x00f08093, 0xf0f0f137, 0x0f010113, 0x0020e733, 0xf0fff3b7, 0x0ff38393, 0x42771c63, 0x00600193, 0xff0100b7, 0xf0008093, 0x0f0f1137, 0xf0f10113, 0x0020e0b3, 0xff1003b7, 0xf0f38393, 0x40709a63, 0x00700193, 0xff0100b7, 0xf0008093, 0x0f0f1137, 0xf0f10113, 0x0020e133, 0xff1003b7, 0xf0f38393, 0x3e711863, 0x00800193, 0xff0100b7, 0xf0008093, 0x0010e0b3, 0xff0103b7, 0xf0038393, 0x3c709a63, 0x00900193, 0x00000213, 0xff0100b7, 0xf0008093, 0x0f0f1137, 0xf0f10113, 0x0020e733, 0x00070313, 0x00120213, 0x00200293, 0xfe5210e3, 0xff1003b7, 0xf0f38393, 0x38731e63, 0x00a00193, 0x00000213, 0x0ff010b7, 0xff008093, 0xf0f0f137, 0x0f010113, 0x0020e733, 0x00000013, 0x00070313, 0x00120213, 0x00200293, 0xfc521ee3, 0xfff103b7, 0xff038393, 0x36731063, 0x00b00193, 0x00000213, 0x00ff00b7, 0x0ff08093, 0x0f0f1137, 0xf0f10113, 0x0020e733, 0x00000013, 0x00000013, 0x00070313, 0x00120213, 0x00200293, 0xfc521ce3, 0x0fff13b7, 0xfff38393, 0x32731063, 0x00c00193, 0x00000213, 0xff0100b7, 0xf0008093, 0x0f0f1137, 0xf0f10113, 0x0020e733, 0x00120213, 0x00200293, 0xfe5212e3, 0xff1003b7, 0xf0f38393, 0x2e771663, 0x00d00193, 0x00000213, 0x0ff010b7, 0xff008093, 0xf0f0f137, 0x0f010113, 0x00000013, 0x0020e733, 0x00120213, 0x00200293, 0xfe5210e3, 0xfff103b7, 0xff038393, 0x2a771a63, 0x00e00193, 0x00000213, 0x00ff00b7, 0x0ff08093, 0x0f0f1137, 0xf0f10113, 0x00000013, 0x00000013, 0x0020e733, 0x00120213, 0x00200293, 0xfc521ee3, 0x0fff13b7, 0xfff38393, 0x26771c63, 0x00f00193, 0x00000213, 0xff0100b7, 0xf0008093, 0x00000013, 0x0f0f1137, 0xf0f10113, 0x0020e733, 0x00120213, 0x00200293, 0xfe5210e3, 0xff1003b7, 0xf0f38393, 0x24771063, 0x01000193, 0x00000213, 0x0ff010b7, 0xff008093, 0x00000013, 0xf0f0f137, 0x0f010113, 0x00000013, 0x0020e733, 0x00120213, 0x00200293, 0xfc521ee3, 0xfff103b7, 0xff038393, 0x20771263, 0x01100193, 0x00000213, 0x00ff00b7, 0x0ff08093, 0x00000013, 0x00000013, 0x0f0f1137, 0xf0f10113, 0x0020e733, 0x00120213, 0x00200293, 0xfc521ee3, 0x0fff13b7, 0xfff38393, 0x1c771463, 0x01200193, 0x00000213, 0x0f0f1137, 0xf0f10113, 0xff0100b7, 0xf0008093, 0x0020e733, 0x00120213, 0x00200293, 0xfe5212e3, 0xff1003b7, 0xf0f38393, 0x18771a63, 0x01300193, 0x00000213, 0xf0f0f137, 0x0f010113, 0x0ff010b7, 0xff008093, 0x00000013, 0x0020e733, 0x00120213, 0x00200293, 0xfe5210e3, 0xfff103b7, 0xff038393, 0x14771e63, 0x01400193, 0x00000213, 0x0f0f1137, 0xf0f10113, 0x00ff00b7, 0x0ff08093, 0x00000013, 0x00000013, 0x0020e733, 0x00120213, 0x00200293, 0xfc521ee3, 0x0fff13b7, 0xfff38393, 0x12771063, 0x01500193, 0x00000213, 0x0f0f1137, 0xf0f10113, 0x00000013, 0xff0100b7, 0xf0008093, 0x0020e733, 0x00120213, 0x00200293, 0xfe5210e3, 0xff1003b7, 0xf0f38393, 0x0e771463, 0x01600193, 0x00000213, 0xf0f0f137, 0x0f010113, 0x00000013, 0x0ff010b7, 0xff008093, 0x00000013, 0x0020e733, 0x00120213, 0x00200293, 0xfc521ee3, 0xfff103b7, 0xff038393, 0x0a771663, 0x01700193, 0x00000213, 0x0f0f1137, 0xf0f10113, 0x00000013, 0x00000013, 0x00ff00b7, 0x0ff08093, 0x0020e733, 0x00120213, 0x00200293, 0xfc521ee3, 0x0fff13b7, 0xfff38393, 0x06771863, 0x01800193, 0xff0100b7, 0xf0008093, 0x00106133, 0xff0103b7, 0xf0038393, 0x04711a63, 0x01900193, 0x00ff00b7, 0x0ff08093, 0x0000e133, 0x00ff03b7, 0x0ff38393, 0x02711c63, 0x01a00193, 0x000060b3, 0x00000393, 0x02709463, 0x01b00193, 0x111110b7, 0x11108093, 0x22222137, 0x22210113, 0x0020e033, 0x00000393, 0x00701463, 0x02301063, 0x0ff0000f, 0x00018063, 0x00119193, 0x0011e193, 0x05d00893, 0x00018513, 0x00000073, 0x0ff0000f, 0x00100193, 0x05d00893, 0x00000513, 0x00000073, 0xc0001073)

let i = 0;
while(!(pass | fail | (i >= 2000)))
  let i = i + 1;
  0 0 0 x x x x
  1 x x x x x x
end while
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*/

/* Test case xor:
clk pass fail pc uop testcase ir

# /home/rj45/Code/rjsc5/tests/xor.hex
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*/

/* Test case slt:
clk pass fail pc uop testcase ir

# /home/rj45/Code/rjsc5/tests/slt.hex
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*/

/* Test case beq:
clk pass fail pc uop testcase ir

# /home/rj45/Code/rjsc5/tests/bge.hex
program(0x00000093, 0x00000113, 0x0020d663, 0x30301863, 0x00301663, 0xfe20dee3, 0x30301263, 0x00300193, 0x00100093, 0x00100113, 0x0020d663, 0x2e301863, 0x00301663, 0xfe20dee3, 0x2e301263, 0x00400193, 0xfff00093, 0xfff00113, 0x0020d663, 0x2c301863, 0x00301663, 0xfe20dee3, 0x2c301263, 0x00500193, 0x00100093, 0x00000113, 0x0020d663, 0x2a301863, 0x00301663, 0xfe20dee3, 0x2a301263, 0x00600193, 0x00100093, 0xfff00113, 0x0020d663, 0x28301863, 0x00301663, 0xfe20dee3, 0x28301263, 0x00700193, 0xfff00093, 0xffe00113, 0x0020d663, 0x26301863, 0x00301663, 0xfe20dee3, 0x26301263, 0x00800193, 0x00000093, 0x00100113, 0x0020d463, 0x00301463, 0x24301663, 0xfe20dee3, 0x00900193, 0xfff00093, 0x00100113, 0x0020d463, 0x00301463, 0x22301863, 0xfe20dee3, 0x00a00193, 0xffe00093, 0xfff00113, 0x0020d463, 0x00301463, 0x20301a63, 0xfe20dee3, 0x00b00193, 0xffe00093, 0x00100113, 0x0020d463, 0x00301463, 0x1e301c63, 0xfe20dee3, 0x00c00193, 0x00000213, 0xfff00093, 0x00000113, 0x1e20d063, 0x00120213, 0x00200293, 0xfe5216e3, 0x00d00193, 0x00000213, 0xfff00093, 0x00000113, 0x00000013, 0x1a20de63, 0x00120213, 0x00200293, 0xfe5214e3, 0x00e00193, 0x00000213, 0xfff00093, 0x00000113, 0x00000013, 0x00000013, 0x1820da63, 0x00120213, 0x00200293, 0xfe5212e3, 0x00f00193, 0x00000213, 0xfff00093, 0x00000013, 0x00000113, 0x1620d863, 0x00120213, 0x00200293, 0xfe5214e3, 0x01000193, 0x00000213, 0xfff00093, 0x00000013, 0x00000113, 0x00000013, 0x1420d463, 0x00120213, 0x00200293, 0xfe5212e3, 0x01100193, 0x00000213, 0xfff00093, 0x00000013, 0x00000013, 0x00000113, 0x1220d063, 0x00120213, 0x00200293, 0xfe5212e3, 0x01200193, 0x00000213, 0xfff00093, 0x00000113, 0x1020d063, 0x00120213, 0x00200293, 0xfe5216e3, 0x01300193, 0x00000213, 0xfff00093, 0x00000113, 0x00000013, 0x0c20de63, 0x00120213, 0x00200293, 0xfe5214e3, 0x01400193, 0x00000213, 0xfff00093, 0x00000113, 0x00000013, 0x00000013, 0x0a20da63, 0x00120213, 0x00200293, 0xfe5212e3, 0x01500193, 0x00000213, 0xfff00093, 0x00000013, 0x00000113, 0x0820d863, 0x00120213, 0x00200293, 0xfe5214e3, 0x01600193, 0x00000213, 0xfff00093, 0x00000013, 0x00000113, 0x00000013, 0x0620d463, 0x00120213, 0x00200293, 0xfe5212e3, 0x01700193, 0x00000213, 0xfff00093, 0x00000013, 0x00000013, 0x00000113, 0x0420d063, 0x00120213, 0x00200293, 0xfe5212e3, 0x01800193, 0x00100093, 0x0000da63, 0x00108093, 0x00108093, 0x00108093, 0x00108093, 0x00108093, 0x00108093, 0x00300393, 0x00709463, 0x02301063, 0x0ff0000f, 0x00018063, 0x00119193, 0x0011e193, 0x05d00893, 0x00018513, 0x00000073, 0x0ff0000f, 0x00100193, 0x05d00893, 0x00000513, 0x00000073, 0xc0001073)

let i = 0;
while(!(pass | fail | (i >= 2000)))
  let i = i + 1;
  0 0 0 x x x x
  1 x x x x x x
end while
0 1 0 x x x x
*/

/* Test case bltu:
clk pass fail pc uop testcase ir

# /home/rj45/Code/rjsc5/tests/jal.hex
program(0x00000093, 0x0100026f, 0x00000013, 0x00000013, 0x0400006f, 0x00000117, 0xff410113, 0x02411a63, 0x00300193, 0x00100093, 0x0140006f, 0x00108093, 0x00108093, 0x00108093, 0x00108093, 0x00108093, 0x00108093, 0x00300393, 0x00709463, 0x02301063, 0x0ff0000f, 0x00018063, 0x00119193, 0x0011e193, 0x05d00893, 0x00018513, 0x00000073, 0x0ff0000f, 0x00100193, 0x05d00893, 0x00000513, 0x00000073, 0xc0001073)

let i = 0;
while(!(pass | fail | (i >= 2000)))
  let i = i + 1;
  0 0 0 x x x x
  1 x x x x x x
end while
0 1 0 x x x x
*/

/* Test case lui:
clk pass fail pc uop testcase ir

# /home/rj45/Code/rjsc5/tests/lui.hex
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*/

/* Test case addi:
clk pass fail pc uop testcase ir

# /home/rj45/Code/rjsc5/tests/addi.hex
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*/

/* Test case andi:
clk pass fail pc uop testcase ir

# /home/rj45/Code/rjsc5/tests/add.hex
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*/

/* Test case ori:
clk pass fail pc uop testcase ir

# /home/rj45/Code/rjsc5/tests/ori.hex
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*/

/* Test case xori:
clk pass fail pc uop testcase ir

# /home/rj45/Code/rjsc5/tests/xori.hex
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*/

/* Test case slti:
clk pass fail pc uop testcase ir

# /home/rj45/Code/rjsc5/tests/slti.hex
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*/

/* Test case bne:
clk pass fail pc uop testcase ir

# /home/rj45/Code/rjsc5/tests/bne.hex
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*/

/* Test case bgeu:
clk pass fail pc uop testcase ir

# /home/rj45/Code/rjsc5/tests/jalr.hex
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*/

/* Test case auipc:
clk pass fail pc uop testcase ir

# /home/rj45/Code/rjsc5/tests/auipc.hex
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*/

/* Test case sub:
clk pass fail pc uop testcase ir

# /home/rj45/Code/rjsc5/tests/andi.hex
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*/

/* Test case sltu:
clk pass fail pc uop testcase ir

# /home/rj45/Code/rjsc5/tests/sltu.hex
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*/

/* Test case sll:
clk pass fail pc uop testcase ir

# /home/rj45/Code/rjsc5/tests/sll.hex
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*/

/* Test case srl:
clk pass fail pc uop testcase ir

# /home/rj45/Code/rjsc5/tests/srl.hex
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*/

/* Test case sra:
clk pass fail pc uop testcase ir

# /home/rj45/Code/rjsc5/tests/xor.hex
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*/

/* Test case blt:
clk pass fail pc uop testcase ir

# /home/rj45/Code/rjsc5/tests/blt.hex
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*/

/* Test case jal:
clk pass fail pc uop testcase ir

# /home/rj45/Code/rjsc5/tests/slt.hex
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*/

/* Test case fence_i:
clk pass fail pc uop testcase ir

# /home/rj45/Code/rjsc5/tests/fence_i.hex
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*/

/* Test case sltiu:
clk pass fail pc uop testcase ir

# /home/rj45/Code/rjsc5/tests/sltiu.hex
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*/

/* Test case slli:
clk pass fail pc uop testcase ir

# /home/rj45/Code/rjsc5/tests/slli.hex
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*/

/* Test case srli:
clk pass fail pc uop testcase ir

# /home/rj45/Code/rjsc5/tests/srli.hex
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*/

/* Test case srai:
clk pass fail pc uop testcase ir

# /home/rj45/Code/rjsc5/tests/xori.hex
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*/

/* Test case bge:
clk pass fail pc uop testcase ir

# /home/rj45/Code/rjsc5/tests/bltu.hex
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*/

/* Test case jalr:
clk pass fail pc uop testcase ir

# /home/rj45/Code/rjsc5/tests/slt.hex
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*/
