// Digital circuit uop_mapper_wrapper.dig as structural Verilog
module uop_mapper_wrapper (
  input  [31:0] inst,
  input  useq,
  output [4:0] uop
);

  wire and_1_out;
  wire [4:0] uop_mapper_1_o0;

  uop_mapper uop_mapper_1 (
    .i28(inst[28]), .i25(inst[25]), .i20(inst[20]), .i14(inst[14]), .i13(inst[13]), .i12(inst[12]),
    .i6(inst[6]), .i5(inst[5]), .i4(inst[4]), .i3(inst[3]), .i2(inst[2]), .iack(useq),
    .o0(uop_mapper_1_o0[4]), .o1(uop_mapper_1_o0[3]), .o2(uop_mapper_1_o0[2]), .o3(uop_mapper_1_o0[1]),
    .o4(uop_mapper_1_o0[0]));
  and and_1 (and_1_out, inst[1], inst[0]);
  Multiplexer #(.Bits(5)) multiplexer_1 (.sel(and_1_out), .in_0({5{1'b0}}), .in_1(uop_mapper_1_o0), .out(uop));
endmodule
